// Logisim project cs158-s2-2.circ as structural Verilog: 1 circuit, main circuit main
module main (
  input  X,
  input  Y,
  input  Z,
  input  Z_2,
  input  X_2,
  input  Y_2,
  output out_7,
  output XY___X_prime_Z
);

  wire and_1_out, and_2_out, and_3_out, and_4_out, and_5_out, not_1_out, not_2_out;

  not not_1 (not_1_out, X);
  not not_2 (not_2_out, X_2);
  and and_1 (and_1_out, X, Y);
  and and_2 (and_2_out, not_1_out, Z);
  and and_3 (and_3_out, Y, Z);
  and and_4 (and_4_out, Z_2, Z_2, not_2_out);
  and and_5 (and_5_out, X_2, Y_2);
  or or_1 (out_7, and_1_out, and_2_out, and_3_out);
  or or_2 (XY___X_prime_Z, and_4_out, and_5_out);

  // Notes on the sheet:
  //   Swaraj Singh
  //   231CS158
  //   S2-2
  //   XY
  //   X'Z
  //   YZ
  //   X'Z
  //   XY
  //   Lab date - 13.08.2024
  //   F2 = XY + X'Z + YZ
endmodule
