// Logisim project CS158-S1-2.circ as structural Verilog: 1 circuit, main circuit main
module main (
  input  A,
  input  B,
  input  C,
  input  D,
  output W,
  output X,
  output Y,
  output Z
);

  wire and_2_out, and_3_out, and_4_out, and_5_out, and_6_out, and_7_out, and_8_out, and_9_out, and_10_out,
       and_11_out, not_1_out, not_3_out, not_4_out;

  not not_1 (not_1_out, A);
  not not_2 (A, B);
  not not_3 (not_3_out, C);
  not not_4 (not_4_out, D);
  and and_1 (W, A, B, D);
  and and_2 (and_2_out, A, A, D);
  and and_3 (and_3_out, A, A, C);
  and and_4 (and_4_out, not_1_out, B, C, not_4_out);
  or or_1 (X, and_2_out, and_3_out, and_4_out);
  and and_5 (and_5_out, not_1_out, B, not_3_out);
  and and_6 (and_6_out, A, A, C);
  or or_2 (Y, and_5_out, and_6_out);
  and and_7 (and_7_out, not_1_out, B, not_3_out, not_4_out);
  and and_8 (and_8_out, not_1_out, A, C, not_4_out);
  and and_9 (and_9_out, A, B, C, D);
  and and_10 (and_10_out, A, A, not_3_out, D);
  and and_11 (and_11_out, A, A, C, not_4_out);
  or or_3 (Z, and_7_out, and_8_out, and_9_out, and_10_out, and_11_out);

  // Notes on the sheet:
  //   ABD
  //   AB'D + AB'C + A'BCD'
  //   A'BC' + AB'C
  //   DDS Lab 5 (Software)
  //   Swaraj Singh
  //   231CS158
  //   27.08.2024
  //   Question S1-2
  //   A'BC'D' + A'B'CD' + ABCD + AB'C'D + AB'CD'
endmodule
