// Logisim project CS158-S2-1.circ as structural Verilog: 1 circuit, main circuit main
module main (
  input  A,
  input  B,
  input  C,
  input  D,
  input  E,
  output Final_Output
);

  wire and_1_out, and_2_out, not_1_out, not_2_out, or_1_out, or_2_out, or_3_out, xor_1_out;

  not not_1 (not_1_out, B);
  not not_2 (not_2_out, D);
  and and_1 (and_1_out, A, D, D);
  or or_1 (or_1_out, not_2_out, E);
  xor xor_1 (xor_1_out, C, E);
  or or_2 (or_2_out, not_1_out, and_1_out);
  or or_3 (or_3_out, A, B);
  and and_2 (and_2_out, A, C);
  and and_3 (Final_Output, or_3_out, and_2_out, xor_1_out, or_1_out, or_2_out);

  // Notes on the sheet:
  //   Swaraj Singh
  //   231 CS 158
  //   Condition 4
  //   Condition 1
  //   Condition 2
  //   Condtion 5
  //   DDS Lab 5 (Software)
  //   Condition 3
  //   27.08.2024
  //   Question S2-2
endmodule
